// Logisim project cpu.circ as structural Verilog: 1 circuit, main circuit main
module main (
  input  [3:0] Rd,
  input  [15:0] in_2,
  input  write
);

  wire clk_out, decoder_1_out0, decoder_1_out1, decoder_1_out2, decoder_1_out3, decoder_1_out4,
       decoder_1_out5, decoder_1_out6, decoder_1_out7, decoder_1_out8, decoder_1_out9, decoder_1_out10,
       decoder_1_out11, decoder_1_out12, decoder_1_out13, decoder_1_out14, decoder_1_out15, undriven;
  wire [15:0] controlled_buffer_1_out, R0_q, R1_q, R2_q, R3_q, R4_q, R5_q, R6_q, R7_q, R8_q;

  Clock clk (.out(clk_out));
  Decoder #(.enable("false"), .select(4)) decoder_1 (
    .out0(decoder_1_out0), .out1(decoder_1_out1), .out2(decoder_1_out2), .out3(decoder_1_out3),
    .out4(decoder_1_out4), .out5(decoder_1_out5), .out6(decoder_1_out6), .out7(decoder_1_out7),
    .out8(decoder_1_out8), .out9(decoder_1_out9), .out10(decoder_1_out10), .out11(decoder_1_out11),
    .out12(decoder_1_out12), .out13(decoder_1_out13), .out14(decoder_1_out14), .out15(decoder_1_out15),
    .sel(Rd));
  assign controlled_buffer_1_out = write ? in_2 : 16'bz;  // Controlled_Buffer controlled_buffer_1
  LED led_1 ();  // open: in
  Register #(.width(16)) R0 (.D(controlled_buffer_1_out), .en(decoder_1_out0), .clk(clk_out), .Q(R0_q), .clr(undriven));
  Register #(.width(16)) R1 (.D(controlled_buffer_1_out), .en(decoder_1_out1), .clk(clk_out), .Q(R1_q), .clr(undriven));
  Register #(.width(16)) R2 (.D(controlled_buffer_1_out), .en(decoder_1_out2), .clk(clk_out), .Q(R2_q), .clr(undriven));
  Register #(.width(16)) R3 (.D(controlled_buffer_1_out), .en(decoder_1_out3), .clk(clk_out), .Q(R3_q), .clr(undriven));
  Register #(.width(16)) R4 (.D(controlled_buffer_1_out), .en(decoder_1_out4), .clk(clk_out), .Q(R4_q), .clr(undriven));
  Register #(.width(16)) R5 (.D(controlled_buffer_1_out), .en(decoder_1_out5), .clk(clk_out), .Q(R5_q), .clr(undriven));
  Register #(.width(16)) R6 (.D(controlled_buffer_1_out), .en(decoder_1_out6), .clk(clk_out), .Q(R6_q), .clr(undriven));
  Register #(.width(16)) R7 (.D(controlled_buffer_1_out), .en(decoder_1_out7), .clk(clk_out), .Q(R7_q), .clr(undriven));
  Register #(.width(16)) R8 (.D(controlled_buffer_1_out), .en(decoder_1_out8), .clk(clk_out), .Q(R8_q), .clr(undriven));
  Register #(.width(16)) R9 (
    .D(controlled_buffer_1_out), .en(decoder_1_out9), .clk(clk_out), .clr(undriven));  // open: Q
  Register #(.width(16)) R10 (
    .D(controlled_buffer_1_out), .en(decoder_1_out10), .clk(clk_out), .clr(undriven));  // open: Q
  Register #(.width(16)) R11 (
    .D(controlled_buffer_1_out), .en(decoder_1_out11), .clk(clk_out), .clr(undriven));  // open: Q
  Register #(.width(16)) R12 (
    .D(controlled_buffer_1_out), .en(decoder_1_out12), .clk(clk_out), .clr(undriven));  // open: Q
  Register #(.width(16)) R13 (
    .D(controlled_buffer_1_out), .en(decoder_1_out13), .clk(clk_out), .clr(undriven));  // open: Q
  Register #(.width(16)) R14 (
    .D(controlled_buffer_1_out), .en(decoder_1_out14), .clk(clk_out), .clr(undriven));  // open: Q
  Register #(.width(16)) R15 (
    .D(controlled_buffer_1_out), .en(decoder_1_out15), .clk(clk_out), .clr(undriven));  // open: Q
  Multiplexer #(.enable("false"), .select(4), .width(16)) multiplexer_1 (
    .in0(R0_q), .in1(R1_q), .in2(R2_q), .in3(R3_q), .in4(R4_q), .in5(R5_q), .in6(R6_q), .in7(R7_q), .in8(R8_q));  // open: in9, in10, in11, in12, in13, in14, in15, out, sel
  Multiplexer #(.enable("false"), .select(4), .width(16)) multiplexer_2 ();  // open: in0, in1, in2, in3, in4, in5, in6, in7, in8, in9, in10, in11, in12, in13, in14, in15, out, sel
endmodule
